# Fritzing sketch Box (saved by Fritzing 0.9.3b)
breadboards: 1

parts:
  J1 = Basic Servo
  S1 = Toggle Switch [package=THT]
  DHT1 = DHT22 Humidity and Temperature Sensor
  Part2 = NRF24L01+ Breakout Board
  Part3 = Bluetooth HC-05 Macho
  Part4 = LCD1602-I2C
  Part5 = MQ-4
  LED1 = smd LED [color="Red (633nm)" package="1206 [SMD]"]
  LED2 = smd LED [color="Red (633nm)" package="1206 [SMD]"]
  Part6 = Arduino Mega 2560 (Rev3)
  J2 = Piezo Speaker
  ESP32_-_Back1 = ESP32 - CAM
  VCC1 = Battery
  R1 = Resistor [tolerance=±5% resistance=1k package="0805 [SMD]"]

nets:
  GND: J1.gnd, DHT1.GND, Part2.GND, Part3.GND, Part4.GND, Part5.GND, LED1.cathode, LED2.cathode, Part6.GND, J2.pin1, ESP32_-_Back1.GND#16, VCC1.-
  VCC: J1.vcc, S1.COM, DHT1.VDD, Part2.VCC, Part3.VCC, Part4.VCC, Part5.VCC, Part6.5V, ESP32_-_Back1.5V
  N1: J1.pulse, Part6.D4_PWM
  N2: S1.L1, VCC1.+
  N3: DHT1.DATA, Part6.A3
  N4: Part2.CE, Part6.D9_PWM
  N5: Part2.CS, Part6.D10_PWM
  N6: Part2.SCK, Part6.D13_PWM
  N7: Part2.MOSI, Part6.D11_PWM
  N8: Part2.MISO, Part6.D12_PWM
  N9: Part3.RXD, Part6.D0_RX0
  N10: Part4.SDA, Part6.D20/SDA
  N11: Part4.SCL, Part6.D21/SCL
  N12: Part5.AO, Part6.A0
  N13: LED1.anode, Part6.D7_PWM
  N14: LED2.anode, Part6.D8_PWM
  N15: Part6.D15/RX3, ESP32_-_Back1.GPIO1_/_TX
  N16: Part6.D14/TX3, ESP32_-_Back1.GPIO3_/_RX
  N17: Part6.D5_PWM, R1.Pin_0
  N18: J2.pin2, R1.Pin_1
  N19: ESP32_-_Back1.GPIO0, ESP32_-_Back1.GND#12

notes:
  I'm still working on camera's code
  MQ-2 "I didn't find fritzing part"

custom parts:
  LCD1602-I2C: A standard character display, usually with 2x16 characters. Comes in many colors with LCM1602 IIC attached.
  ESP32 - CAM: The ESP32-CAM has a very competitive small-size camera module that can operate independently as a minimum system with a footprint of only 27*40.5*4.5mm and a deep sleep current of up to 6mA.
  Battery: Your standard 2x 18650 battery pack (7,4 Volts)
